# Fritzing sketch water (saved by Fritzing 1.0.4)
breadboards: 1

parts:
  Chirp!_Soil_Moisture_Sensor1 = Chirp! Soil Moisture Sensor v2.7.3
  A1 = Particle - Photon2
  Relay1 = Relay - 6 pins [package="DIP (Dual Inline) [THT]"]
  Part3 = prefix101282
  OLED_I2C2 = OLED 128x64 I2C Monochrome Display
  Part4 = BME280 Breakout
  WATER_PUMP2 = water pump/motor
  R1 = Resistor [tolerance=±5% resistance=220 package="1206 [SMD]"]
  R2 = Resistor [tolerance=±5% power=0.25W resistance=220 package=THT]
  Q1 = PNP-Transistor [package="SOT-23 [SMD]"]

nets:
  VCC: Chirp!_Soil_Moisture_Sensor1.Pin_1, A1.Pin_2, A1.Pin_31, Relay1.VCC, Part3.connector5, OLED_I2C2.VDD, Part4.3.3V
  N1: Chirp!_Soil_Moisture_Sensor1.pin_3, A1.Pin_5
  GND: Chirp!_Soil_Moisture_Sensor1.pin_5, A1.Pin_4, A1.Pin_32, A1.Pin_35, Relay1.GND, Part3.connector6, OLED_I2C2.GND, Part4.GND, WATER_PUMP2.pin_2, R1.Pin_0, R1.Pin_1, Q1.1
  N2: A1.Pin_13, Q1.0
  N3: Relay1.IN, R2.Pin_1, Q1.2
  N4: Relay1.COM, WATER_PUMP2.pin_1

custom parts:
  Particle - Photon2: The Photon 2 is a microcontroller and Wi-Fi networking developed by particle. Features: 802.11a/b/g/n Wi-Fi, 2.4 GHz and 5 GHz Integrated PCB antenna Integrated U.FL connector for external antenna Integrated RF switch BLE 5 using same antenna as Wi-Fi Realtek RTL8721DM MCU ARM Cortex M33 CPU, 200 MHz 2048 KB (2 MB) user application maximum size 3072 KB (3 MB) of RAM available to user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
  Relay - 6 pins: A DIP stand-in part for whatever IC you want. With 6 pins on a 900mil dual inline package (DIP) footprint.
  water pump/motor: WATER PUMP BY ARDUBLOCKTR
